// Logisim project LICRouletteDisplay.circ as structural Verilog: 13 circuits, main circuit main
module main (
  input  Kscan,
  output K0,
  output K1,
  output K2,
  output K3,
  output Kpress
);

  wire clock_1_out, dec_1__0, dec_1__1, dec_1__2, n4x4_matrix_keyboard_1_p3, not_1_out, not_2_out, not_4_out,
       not_5_out, not_6_out, not_7_out, penc_1_y0, penc_1_y1, pull_resistor_1_node, pull_resistor_2_node,
       pull_resistor_3_node, pull_resistor_4_node;

  Pull_Resistor #(.pull(1)) pull_resistor_1 (.node(pull_resistor_1_node));
  Clock clock_1 (.out(clock_1_out));
  Pull_Resistor #(.pull(1)) pull_resistor_2 (.node(pull_resistor_2_node));
  Pull_Resistor #(.pull(1)) pull_resistor_3 (.node(pull_resistor_3_node));
  Pull_Resistor #(.pull(1)) pull_resistor_4 (.node(pull_resistor_4_node));
  CONT cont_1 (.Clock(clock_1_out), .CE(Kscan), .Q0(K0), .Q1(K1));  // open: in_3, in_4
  DEC dec_1 (.S1(K1), .S0(K0), ._0(dec_1__0), ._1(dec_1__1), ._2(dec_1__2));
  not not_1 (not_1_out, dec_1__0);
  not not_2 (not_2_out, dec_1__1);
  // _4x4_Matrix_Keyboard 4x4_matrix_keyboard_1: pin names not known; wires that end beside it: not_1_out, not_2_out, n4x4_matrix_keyboard_1_p3
  not not_3 (n4x4_matrix_keyboard_1_p3, dec_1__2);
  not not_4 (not_4_out, pull_resistor_3_node);
  not not_5 (not_5_out, pull_resistor_4_node);
  not not_6 (not_6_out, pull_resistor_2_node);
  not not_7 (not_7_out, pull_resistor_1_node);
  PENC penc_1 (
    ._0(not_4_out), ._1(not_5_out), ._2(not_6_out), ._3(not_7_out), .Y1(penc_1_y1), .Y0(penc_1_y0),
    .GS(Kpress));  // open: _0_2, Y0_2, _1_2, _2_2, Y1_2, _3_2, GS_2
  REG reg_1 (.Clock(Kscan), .Y0(penc_1_y0), .Y1(penc_1_y1), .Q0(K2), .Q1(K3));
endmodule

module PENC (
  input  _0,
  input  _1,
  input  _2,
  input  _3,
  input  _0_2,
  input  _1_2,
  input  _2_2,
  input  _3_2,
  output Y0,
  output Y1,
  output GS,
  output Y0_2,
  output Y1_2,
  output GS_2
);

  wire and_1_out, and_3_out, and_4_out;

  or or_1 (GS, _0, _1, _2, _3);
  or or_2 (GS_2, _0_2, _1_2, _2_2, _3_2);
  and and_1 (and_1_out, _1, ~_2);  // AND_Gate
  and and_2 (Y1_2, ~_0_2, ~_1_2);  // AND_Gate
  or or_3 (Y0, _3, and_1_out);
  or or_4 (Y1, _2, _3);
  and and_3 (and_3_out, ~_0_2, _1_2);  // AND_Gate
  or or_5 (Y0_2, and_3_out, and_4_out);
  and and_4 (and_4_out, ~_0_2, ~_2_2, _3_2);  // AND_Gate

  // Notes on the sheet:
  //   PRIORITY HIGH
  //   PRIORITY LOW
endmodule

module DEC (
  input  S1,
  input  S0,
  output _0,
  output _1,
  output _2
);

  and and_1 (_0, ~S1, ~S0);  // AND_Gate
  and and_2 (_1, ~S1, S0);  // AND_Gate
  and and_3 (_2, S1, ~S0);  // AND_Gate
endmodule

module CONT (
  input  Clock,
  input  CE,
  input  in_3,
  input  in_4,
  output Q0,
  output Q1
);

  wire and_1_out, and_2_out, d_ff_1_qn, xor_1_out;

  and and_1 (and_1_out, Clock, CE);
  and and_2 (and_2_out, d_ff_1_qn, ~Q1);  // AND_Gate
  D_Flip_Flop d_ff_1 (.clk(and_1_out), .D(and_2_out), .Q(Q0), .Qn(d_ff_1_qn));  // open: preset, en, reset
  D_Flip_Flop d_ff_2 (.clk(and_1_out), .D(Q0), .Q(Q1));  // open: Qn, preset, en, reset
  xor xor_1 (xor_1_out, in_3, in_4);
endmodule

module REG (
  input  Clock,
  input  Y0,
  input  Y1,
  output Q0,
  output Q1
);

  wire d_ff_1_qn;

  D_Flip_Flop d_ff_1 (.clk(Clock), .D(Y0), .Q(Q0), .Qn(d_ff_1_qn));  // open: preset, en, reset
  D_Flip_Flop d_ff_2 (.clk(Clock), .D(Y1), .Q(Q1));  // open: Qn, preset, en, reset
endmodule

module Pal_com_control (
  input  Kack,
  output Kval,
  output out_3,
  output out_4,
  output out_5,
  output out_6,
  output K0,
  output K1,
  output K2,
  output K3
);

  wire atf750c_1_p10, atf750c_1_p11, clock_1_out, n4x4_matrix_keyboard_1_p1, n4x4_matrix_keyboard_1_p2,
       n4x4_matrix_keyboard_1_p3;

  Pull_Resistor #(.pull(1)) pull_resistor_1 (.node(K3));
  Clock clock_1 (.out(clock_1_out));
  Pull_Resistor #(.pull(1)) pull_resistor_2 (.node(K2));
  Pull_Resistor #(.pull(1)) pull_resistor_3 (.node(K1));
  Pull_Resistor #(.pull(1)) pull_resistor_4 (.node(K0));
  // _4x4_Matrix_Keyboard 4x4_matrix_keyboard_1: pin names not known; wires that end beside it: n4x4_matrix_keyboard_1_p1, n4x4_matrix_keyboard_1_p2, n4x4_matrix_keyboard_1_p3
  // ATF750c atf750c_1: pin names not known; wires that end beside it: clock_1_out, Kack, K0, K1, K2, K3, 1'b0, 1'b1, Kval, atf750c_1_p10, atf750c_1_p11, out_3, out_4, out_5, out_6, n4x4_matrix_keyboard_1_p3, n4x4_matrix_keyboard_1_p2, n4x4_matrix_keyboard_1_p1, atf750c_1_p10, atf750c_1_p11
endmodule

module PAL_keyboard (
  input  Kscan,
  output out_2,
  output Kpress,
  output out_4,
  output out_5,
  output out_6,
  output K0,
  output K1,
  output K2,
  output K3
);

  wire atf750c_1_p14, atf750c_1_p15, atf750c_1_p16, clock_1_out;

  Clock clock_1 (.out(clock_1_out));
  Pull_Resistor #(.pull(1)) pull_resistor_1 (.node(K3));
  Pull_Resistor #(.pull(1)) pull_resistor_2 (.node(K0));
  Pull_Resistor #(.pull(1)) pull_resistor_3 (.node(K1));
  Pull_Resistor #(.pull(1)) pull_resistor_4 (.node(K2));
  // ATF750c atf750c_1: pin names not known; wires that end beside it: clock_1_out, Kscan, K0, K1, K2, K3, 1'b0, 1'b1, Kpress, out_2, out_4, out_5, out_6, atf750c_1_p14, atf750c_1_p15, atf750c_1_p16
  // _4x4_Matrix_Keyboard 4x4_matrix_keyboard_1: pin names not known; wires that end beside it: atf750c_1_p16, atf750c_1_p15, atf750c_1_p14
endmodule

module PAL_BUFFER (
  input  Kack,
  output out_2,
  output out_3,
  output out_4,
  output Kscan,
  output out_6,
  output Dval,
  output K0,
  output K1,
  output K2,
  output K3
);

  wire atf750c_1_p14, atf750c_1_p15, atf750c_1_p16, clock_1_out;

  Clock clock_1 (.out(clock_1_out));
  Pull_Resistor #(.pull(1)) pull_resistor_1 (.node(K3));
  Pull_Resistor #(.pull(1)) pull_resistor_2 (.node(K2));
  Pull_Resistor #(.pull(1)) pull_resistor_3 (.node(K1));
  Pull_Resistor #(.pull(1)) pull_resistor_4 (.node(K0));
  // ATF750c atf750c_1: pin names not known; wires that end beside it: clock_1_out, Kack, K0, K1, K2, K3, 1'b1, out_2, out_3, out_4, out_6, Kscan, Dval, atf750c_1_p14, atf750c_1_p15, atf750c_1_p16
  // _4x4_Matrix_Keyboard 4x4_matrix_keyboard_1: pin names not known; wires that end beside it: atf750c_1_p16, atf750c_1_p15, 1'b0, atf750c_1_p14
endmodule

module counter (
  input  in_1,
  input  Kscan,
  input  in_3,
  output Q0,
  output Q1
);

  wire and_1_out, clock_1_out, xor_1_out, xor_2_out;

  Clock clock_1 (.out(clock_1_out));
  xor xor_1 (xor_1_out, Kscan, Q0);
  D_Flip_Flop d_ff_1 (.clk(clock_1_out), .D(xor_1_out), .Q(Q0), .reset(in_3));  // open: Qn, preset, en
  and and_1 (and_1_out, Q0, Kscan);
  D_Flip_Flop d_ff_2 (.clk(clock_1_out), .D(xor_2_out), .Q(Q1), .reset(in_3));  // open: Qn, preset, en
  xor xor_2 (xor_2_out, and_1_out, Q1);
endmodule

module LCD (
  input  d0,
  input  d1,
  input  d2,
  input  d3,
  input  d4,
  input  ph,
  input  wr,
  input  in_8,
  input  in_9,
  input  in_10,
  input  in_11,
  input  in_12,
  input  in_13
);

  wire atf750c_1_p12, atf750c_1_p13, atf750c_1_p14, atf750c_1_p15, atf750c_1_p16, atf750c_1_p17,
       atf750c_1_p18, atf750c_1_p19;

  // LCD_16x2 lcd_16x2_1: pin names not known; wires that end beside it: in_8, in_9, in_10, in_11
  // ATF750c atf750c_1: pin names not known; wires that end beside it: 1'b1, 1'b0, d0, d1, d2, d3, d4, ph, wr, 1'b0, 1'b1, atf750c_1_p12, atf750c_1_p13, atf750c_1_p14, atf750c_1_p15, atf750c_1_p16, atf750c_1_p17, atf750c_1_p18, atf750c_1_p19
  _7_Segment_Display u_7_segment_display_1 (
    .g(atf750c_1_p14), .f(atf750c_1_p13), .a(atf750c_1_p16), .b(atf750c_1_p17), .e(atf750c_1_p12),
    .d(atf750c_1_p15), .c(atf750c_1_p18), .dp(atf750c_1_p19));
endmodule

module ALL (
  input  M,
  output Kscan
);

  wire atf750c_1_p2, atf750c_1_p7, atf750c_1_p9, atf750c_1_p10, atf750c_1_p11, atf750c_1_p12, atf750c_1_p14,
       atf750c_1_p18, atf750c_2_p10, atf750c_2_p11, atf750c_2_p12, atf750c_2_p13, atf750c_2_p14,
       atf750c_2_p15, atf750c_2_p16, clock_1_out, lcd_16x2_1_p1, lcd_16x2_1_p2, lcd_16x2_1_p3, lcd_16x2_1_p4,
       n4x4_matrix_keyboard_1_p1, n4x4_matrix_keyboard_1_p2, n4x4_matrix_keyboard_1_p4, pull_resistor_1_node,
       pull_resistor_2_node, pull_resistor_3_node, pull_resistor_4_node;

  // LCD_16x2 lcd_16x2_1: pin names not known; wires that end beside it: lcd_16x2_1_p1, lcd_16x2_1_p2, lcd_16x2_1_p3, lcd_16x2_1_p4
  Clock clock_1 (.out(clock_1_out));
  Pull_Resistor #(.pull(1)) pull_resistor_1 (.node(pull_resistor_1_node));
  Pull_Resistor #(.pull(1)) pull_resistor_2 (.node(pull_resistor_2_node));
  Pull_Resistor #(.pull(1)) pull_resistor_3 (.node(pull_resistor_3_node));
  Pull_Resistor #(.pull(1)) pull_resistor_4 (.node(pull_resistor_4_node));
  // _4x4_Matrix_Keyboard 4x4_matrix_keyboard_1: pin names not known; wires that end beside it: n4x4_matrix_keyboard_1_p1, n4x4_matrix_keyboard_1_p2, 1'b0, n4x4_matrix_keyboard_1_p4, n4x4_matrix_keyboard_1_p1, pull_resistor_1_node, pull_resistor_2_node, pull_resistor_4_node, pull_resistor_3_node
  // ATF750c atf750c_1: pin names not known; wires that end beside it: clock_1_out, atf750c_1_p2, pull_resistor_1_node, pull_resistor_2_node, pull_resistor_4_node, pull_resistor_3_node, atf750c_1_p7, 1'b1, atf750c_1_p9, atf750c_1_p10, atf750c_1_p11, atf750c_1_p12, Kscan, atf750c_1_p14, n4x4_matrix_keyboard_1_p4, n4x4_matrix_keyboard_1_p2, 1'b0, atf750c_1_p18, 1'b0, 1'b1, 1'b0
  // ATF750c atf750c_2: pin names not known; wires that end beside it: lcd_16x2_1_p4, lcd_16x2_1_p3, lcd_16x2_1_p2, lcd_16x2_1_p1, atf750c_1_p18, 1'b0, atf750c_1_p7, 1'b0, 1'b1, atf750c_2_p10, atf750c_2_p11, atf750c_2_p12, atf750c_2_p13, atf750c_2_p14, atf750c_2_p15, atf750c_2_p16
  _7_Segment_Display u_7_segment_display_1 (
    .g(atf750c_2_p12), .f(atf750c_2_p11), .a(atf750c_2_p14), .b(atf750c_2_p15), .e(atf750c_2_p10),
    .d(atf750c_2_p13), .c(atf750c_2_p16));  // open: dp
  // UsbPort usbport_1: pin names not known; wires that end beside it: atf750c_1_p2, atf750c_1_p7, atf750c_1_p18, lcd_16x2_1_p1, lcd_16x2_1_p2, lcd_16x2_1_p3, lcd_16x2_1_p4, M
endmodule

module ALL_With_SOC (
  input  M,
  output Kscan
);

  wire atf750c_2_p10, atf750c_2_p11, atf750c_2_p12, atf750c_2_p13, atf750c_2_p14, atf750c_2_p15,
       atf750c_2_p16, C0, C1, clock_1_out, clock_2_out, Dval, L0, L1, n4x4_matrix_keyboard_1_p1,
       n4x4_matrix_keyboard_1_p2, n4x4_matrix_keyboard_1_p4, o0, o1, o2, o3, o4, o5, o6, o7,
       pull_resistor_1_node, pull_resistor_2_node, pull_resistor_3_node, pull_resistor_4_node, S0, S1, S2,
       S3, S4, Wr, Wrl;

  // LCD_16x2 lcd_16x2_1: pin names not known; wires that end beside it: S0, S1, S2, S3
  Clock clock_1 (.out(clock_1_out));
  Pull_Resistor #(.pull(1)) pull_resistor_1 (.node(pull_resistor_1_node));
  Pull_Resistor #(.pull(1)) pull_resistor_2 (.node(pull_resistor_2_node));
  Pull_Resistor #(.pull(1)) pull_resistor_3 (.node(pull_resistor_3_node));
  Pull_Resistor #(.pull(1)) pull_resistor_4 (.node(pull_resistor_4_node));
  // _4x4_Matrix_Keyboard 4x4_matrix_keyboard_1: pin names not known; wires that end beside it: n4x4_matrix_keyboard_1_p1, n4x4_matrix_keyboard_1_p2, 1'b0, n4x4_matrix_keyboard_1_p4, n4x4_matrix_keyboard_1_p1, pull_resistor_4_node, pull_resistor_3_node, pull_resistor_1_node, pull_resistor_2_node
  // ATF750c atf750c_1: pin names not known; wires that end beside it: clock_1_out, o7, pull_resistor_4_node, pull_resistor_3_node, pull_resistor_1_node, pull_resistor_2_node, Wrl, 1'b1, L0, L1, C0, C1, Kscan, Dval, n4x4_matrix_keyboard_1_p4, n4x4_matrix_keyboard_1_p2, 1'b0, S4, 1'b0, 1'b1, 1'b0
  Clock clock_2 (.out(clock_2_out));
  // UsbPort usbport_1: pin names not known; wires that end beside it: o7, o6, o5, o4, o3, o2, o1, o0, M
  // ATF750c atf750c_2: pin names not known; wires that end beside it: S0, S1, S2, S3, S4, 1'b0, Wr, 1'b0, 1'b1, atf750c_2_p10, atf750c_2_p11, atf750c_2_p12, atf750c_2_p13, atf750c_2_p14, atf750c_2_p15, atf750c_2_p16
  // ATF750c atf750c_3: pin names not known; wires that end beside it: o3, o2, o1, clock_2_out, 1'b0, 1'b1, Wr, Wrl, S4, S3, S2, S1, S0
  _7_Segment_Display u_7_segment_display_1 (
    .g(atf750c_2_p12), .f(atf750c_2_p11), .a(atf750c_2_p14), .b(atf750c_2_p15), .e(atf750c_2_p10),
    .d(atf750c_2_p13), .c(atf750c_2_p16));  // open: dp
endmodule

module testing_stuff (
  input  SS,
  input  SCLK,
  input  DATA
);

  wire clock_1_out, S0, S1, S2, S3, S4, Wr, Wrl;

  // LCD_16x2 lcd_16x2_1: pin names not known; wires that end beside it: S4, S3, S2, S0, S1
  Clock clock_1 (.out(clock_1_out));
  // ATF750c atf750c_1: pin names not known; wires that end beside it: SS, SCLK, DATA, clock_1_out, 1'b0, 1'b1, Wr, Wrl, S4, S3, S2, S1, S0
endmodule
